# Fritzing sketch Temp and Humidity (saved by Fritzing 0.9.4)
breadboards: 1

parts:
  Part1 = Arduino Uno (Rev3) - ICSP
  U1 = POT [package=pot_alpha_rv16af-20]
  U3 = LCD-16X2 [package=lcd-16x2]
  R1 = Resistor [tolerance=±5% resistance=220 package="2010 [SMD]"]
  DHT1 = DHT11 Humitidy and Temperature Sensor
  R2 = Resistor [tolerance=±5% resistance=10k package="2010 [SMD]"]

nets:
  VDD: Part1.D8, Part1.5V, U1.E, U3.VDD, U3.A, R1.Pin_0, R1.Pin_1, DHT1.VDD, R2.Pin_1
  N1: Part1.D11_PWM/MOSI, DHT1.DATA, R2.Pin_0
  N2: Part1.D2, U3.RS
  N3: Part1.D3_PWM, U3.E
  N4: Part1.D4, U3.DB4
  N5: Part1.D5_PWM, U3.DB5
  N6: Part1.D6_PWM, U3.DB6
  N7: Part1.D7, U3.DB7
  GND: Part1.GND, U1.A, U3.VSS, U3.R_W, U3.K, DHT1.GND
  N8: U1.S, U3.VO

custom parts:
  DHT11 Humitidy and Temperature Sensor: DHT11 Humidity and Temperature Sensor
